# Fritzing sketch thingie (saved by Fritzing 0.7.12b)
breadboards: 1

parts:
  Arduino2 = Arduino Fio
  S2 = Square Pushbutton
  LED1 = RGB LED (com. anode, rbg) [package="5 mm [THT]"]
  S3 = Square Pushbutton
  PIR1 = PIR sensor
  R1 = Resistor [tolerance=±5% resistance=220 package=THT]

nets:
  3V3: Arduino2.3V3, S2.leg0, S3.leg0, PIR1.VDD
  GND: Arduino2.GND, LED1.common_anode, PIR1.GND
  N1: Arduino2.D9, LED1.red_cathode
  N2: Arduino2.D10, LED1.blue_cathode
  N3: Arduino2.D11, LED1.green_cathode
  N4: Arduino2.D12, S3.leg1
  N5: Arduino2.D13, S2.leg1
  N6: PIR1.SIG, R1.Pin_0
